# Fritzing sketch schematic_diagram (saved by Fritzing 0.9.0b)

parts:
  Teensy_3_1 = Teensy 3.1
  T1 = LM35 Temperature Sensor [package="TO92 [THT]"]
  RHT1 = Humidity and Temperature Sensor RHT03
  R1 = Photocell (LDR) [package=THT]
  R2 = Temperature Sensor (Thermistor) [thermistor_type=NTC package=THT]
  U1 = ESP8266 WiFi Module [part_number=ESP8266]
  Q1 = TRANSISTOR_NPN [package=to-92-ammo]
  R3 = Resistor [package="2512 [SMD]"]
  R5 = Resistor [package="2512 [SMD]"]
  R6 = Resistor [package="2512 [SMD]"]
  R7 = Resistor [package="2512 [SMD]"]
  R8 = Resistor [package="2512 [SMD]"]  # not connected
  U2 = TEMPERATURE-SENSOR [package=to-92]
  R9 = Resistor [package="2512 [SMD]"]
  R4 = Resistor [package="2512 [SMD]"]

nets:
  N1: Teensy_3_1.D2, RHT1.Data-signal
  N2: Teensy_3_1.D9, U1.TXD
  N3: Teensy_3_1.D10, U1.RXD, U1.RST
  N4: Teensy_3_1.A0/D14, R2.pin_0, R4.Pin_0
  N5: Teensy_3_1.A1/D15, U2.GND, R9.Pin_1
  N6: Teensy_3_1.A2/D16, R1.pin_1, R3.Pin_0
  N7: Teensy_3_1.A3/D17, T1.Vout, R5.Pin_0
  GND: Teensy_3_1.AGND, T1.GND, U1.GND, R3.Pin_1, R4.Pin_1
  N8: Teensy_3_1.Vin, Q1.E
  N9: R1.pin_0, R2.pin_1, R9.Pin_0
  N10: U1.VCC, Q1.C, R6.Pin_1
  N11: U1.CH_PD, R7.Pin_1

notes:
  ESP8266-01
  NTC Thermistor 5k ohms
  KTY81 PTC Thermistor 1k ohm
  LDR
  LM35
  DHT11
  Teensy LC
  BC548 NPN
  10k ohm
  1k ohm
  4k7 ohm
  390 ohm
  680 ohm

custom parts:
  ESP8266 WiFi Module: Generic WiFi Module based on the ESP8266 with onboard PCB antenna and UART communications
